// Logisim project CPU.circ as structural Verilog: 1 circuit, main circuit main
module main (
  input  Rst
);

  wire Clk_out;
  wire [7:0] adder_1_out, PC_q;
  wire [31:0] ram_1_dout;

  Clock Clk (.out(Clk_out));
  Register PC (.D(adder_1_out), .en(1'b1), .clk(Clk_out), .Q(PC_q), .clr(Rst));
  Adder adder_1 (.a(PC_q), .b(8'h1), .out(adder_1_out), .cin(1'b0));  // open: cout
  RAM #(.dataWidth(32)) ram_1 (.addr(PC_q), .we(1'b0), .oe(1'b1), .clk(Clk_out), .dout(ram_1_dout));  // open: din
endmodule
